// Logisim project WITCPU.circ as structural Verilog: 7 circuits, main circuit WITCPU
module Registers (
  input  in_1,
  input  [3:0] in_2,
  input  [3:0] in_3,
  input  [15:0] Rd,
  input  [3:0] in_5,
  output [15:0] Rx,
  output [15:0] Ry
);

  wire demultiplexer_1_out0, demultiplexer_1_out1, demultiplexer_1_out2, demultiplexer_1_out3,
       demultiplexer_1_out4, demultiplexer_1_out5, demultiplexer_1_out6, demultiplexer_1_out7,
       demultiplexer_1_out8, demultiplexer_1_out9, demultiplexer_1_out10, demultiplexer_1_out11,
       demultiplexer_1_out12, demultiplexer_1_out13, demultiplexer_1_out14, demultiplexer_1_out15;
  wire [15:0] R0_q, R1_q, R2_q, R3_q, R4_q, R5_q, R6_q, R7_q, R8_q, R9_q, Ra_q, Rb_q, Rc_q, Rd_q, Re_q, Rf_q;

  Demultiplexer #(.select(4)) demultiplexer_1 (
    .out0(demultiplexer_1_out0), .out1(demultiplexer_1_out1), .out2(demultiplexer_1_out2),
    .out3(demultiplexer_1_out3), .out4(demultiplexer_1_out4), .out5(demultiplexer_1_out5),
    .out6(demultiplexer_1_out6), .out7(demultiplexer_1_out7), .out8(demultiplexer_1_out8),
    .out9(demultiplexer_1_out9), .out10(demultiplexer_1_out10), .out11(demultiplexer_1_out11),
    .out12(demultiplexer_1_out12), .out13(demultiplexer_1_out13), .out14(demultiplexer_1_out14),
    .out15(demultiplexer_1_out15), .in(in_1), .sel(in_3));  // open: en
  Register #(.width(16)) R0 (.D(Rd), .Q(R0_q), .clk(demultiplexer_1_out0));  // open: en, clr
  Register #(.width(16)) R2 (.D(Rd), .Q(R2_q), .clk(demultiplexer_1_out2));  // open: en, clr
  Register #(.width(16)) R1 (.D(Rd), .Q(R1_q), .clk(demultiplexer_1_out1));  // open: en, clr
  Register #(.width(16)) R4 (.D(Rd), .Q(R4_q));  // open: en, clk, clr
  Register #(.width(16)) R5 (.D(Rd), .Q(R5_q), .clk(demultiplexer_1_out5));  // open: en, clr
  Register #(.width(16)) R3 (.D(Rd), .Q(R3_q), .clk(demultiplexer_1_out3));  // open: en, clr
  Register #(.width(16)) R6 (.D(Rd), .Q(R6_q));  // open: en, clk, clr
  Register #(.width(16)) R7 (.D(Rd), .Q(R7_q), .clk(demultiplexer_1_out7));  // open: en, clr
  Register #(.width(16)) R8 (.D(Rd), .Q(R8_q));  // open: en, clk, clr
  Register #(.width(16)) R9 (.D(Rd), .Q(R9_q), .clk(demultiplexer_1_out9));  // open: en, clr
  Register #(.width(16)) Ra (.D(Rd), .Q(Ra_q), .clk(demultiplexer_1_out10));  // open: en, clr
  Register #(.width(16)) Rb (.D(Rd), .Q(Rb_q), .clk(demultiplexer_1_out11));  // open: en, clr
  Register #(.width(16)) Rc (.D(Rd), .Q(Rc_q));  // open: en, clk, clr
  Register #(.width(16)) u_Rd (.D(Rd), .Q(Rd_q), .clk(demultiplexer_1_out13));  // open: en, clr
  Register #(.width(16)) Re (.D(Rd), .Q(Re_q), .clk(demultiplexer_1_out14));  // open: en, clr
  Register #(.width(16)) Rf (.D(Rd), .Q(Rf_q), .clk(demultiplexer_1_out15));  // open: en, clr
  Multiplexer #(.select(4), .width(16)) multiplexer_1 (
    .in0(R0_q), .in1(R1_q), .in2(R2_q), .in3(R3_q), .in4(R4_q), .in5(R5_q), .in6(R6_q), .in7(R7_q),
    .in8(R8_q), .in9(R9_q), .in10(Ra_q), .in11(Rb_q), .in12(Rc_q), .in13(Rd_q), .in14(Re_q), .in15(Rf_q),
    .out(Rx), .sel(in_2));  // open: en
  Multiplexer #(.select(4), .width(16)) multiplexer_2 (
    .in0(R0_q), .in1(R1_q), .in2(R2_q), .in3(R3_q), .in4(R4_q), .in5(R5_q), .in6(R6_q), .in7(R7_q),
    .in8(R8_q), .in9(R9_q), .in10(Ra_q), .in11(Rb_q), .in12(Rc_q), .in13(Rd_q), .in14(Re_q), .in15(Rf_q),
    .out(Ry), .sel(in_5));  // open: en
endmodule

module WITCPU (
  input  in_1
);

  wire and_1_out, and_2_out, Bus_Controller_p7, Bus_Controller_p8, Bus_Controller_p9, Bus_Controller_p10,
       clock_1_out, not_1_out, t_ff_1_q;
  wire [3:0] Decoder_oo1, Decoder_oo2, Decoder_oo3, Decoder_opcode;
  wire [7:0] Bus_Controller_p6, Decoder_output, multiplexer_1_out, PC_Controller_output, register_2_q;
  wire [15:0] ALU_d, register_1_q, Registers_rx, Registers_ry;

  and and_1 (and_1_out, clock_1_out, not_1_out);
  not not_1 (not_1_out, clock_1_out);
  Register #(.width(16)) register_1 (.Q(register_1_q), .clr(and_1_out));  // open: D, en, clk
  Decoder Decoder (
    .Input(register_1_q), .Opcode(Decoder_opcode), .Output(Decoder_output), .OO1(Decoder_oo1),
    .OO2(Decoder_oo2), .OO3(Decoder_oo3));
  Registers Registers (
    .in_1(Bus_Controller_p8), .in_3(Decoder_oo1), .Rd(ALU_d), .Rx(Registers_rx), .in_2(Decoder_oo2),
    .Ry(Registers_ry), .in_5(Decoder_oo3));
  Multiplexer #(.width(8)) multiplexer_1 (
    .in0(Bus_Controller_p6), .in1(register_2_q), .out(multiplexer_1_out), .sel(t_ff_1_q));  // open: en
  Clock clock_1 (.out(clock_1_out));
  T_Flip_Flop t_ff_1 (.clk(clock_1_out), .T(1'b1), .Q(t_ff_1_q));  // open: Qn, preset, reset, en
  and and_2 (and_2_out, clock_1_out, clock_1_out);
  ALU ALU (
    .X(Registers_rx), .Y(Registers_ry), .MOV(Decoder_output), .Opcode(Decoder_opcode),
    .in_3(Bus_Controller_p7), .D(ALU_d));
  RAM_part #(.dataWidth(16), .bus("separate")) ram_1 (
    .addr(multiplexer_1_out), .din(Registers_rx), .data(ALU_d), .str(Bus_Controller_p10), .sel(1'b1),
    .clk(clock_1_out), .ld(Bus_Controller_p9), .clr(in_1));
  PC_Controller PC_Controller (
    .Rx(Registers_rx), .Input(Decoder_output), .PC_input(register_2_q), .Opcode(Decoder_opcode),
    .Output(PC_Controller_output));  // open: in_4, in_5
  Register register_2 (.D(PC_Controller_output), .Q(register_2_q), .clr(and_2_out));  // open: en, clk
  // Bus_Controller Bus_Controller: pin names not known; wires that end beside it: Decoder_opcode, Registers_rx, Decoder_output, clock_1_out, t_ff_1_q, Bus_Controller_p6, Bus_Controller_p7, Bus_Controller_p8, Bus_Controller_p9, Bus_Controller_p10
endmodule

module ALU (
  input  [7:0] MOV,
  input  [3:0] Opcode,
  input  in_3,
  output [15:0] X,
  output [15:0] D,
  output [15:0] Y
);

  wire [3:0] controlled_buffer_1_out;
  wire [7:0] undriven;
  wire [15:0] adder_1_out, and_1_out, divider_1_out, multiplier_1_out, or_1_out, register_1_q, register_2_q,
       subtractor_1_out, xor_1_out;

  Register #(.width(16)) register_1 (.D(X), .Q(register_1_q));  // open: en, clk, clr
  Register #(.width(16)) register_2 (.D(Y), .Q(register_2_q));  // open: en, clk, clr
  Subtractor #(.width(16)) subtractor_1 (
    .a(register_1_q), .b(register_2_q), .out(subtractor_1_out));  // open: bin, bout
  Multiplier #(.width(16)) multiplier_1 (
    .a(register_1_q), .b(register_2_q), .out(multiplier_1_out));  // open: cin, cout
  Divider #(.width(16)) divider_1 (.a(register_1_q), .b(register_2_q), .out(divider_1_out));  // open: upper, rem
  assign and_1_out = register_1_q & register_2_q;  // AND_Gate and_1, 16 bits wide
  assign controlled_buffer_1_out = in_3 ? Opcode : 4'bz;  // Controlled_Buffer controlled_buffer_1
  Adder #(.width(16)) adder_1 (.a(register_1_q), .b(register_2_q), .out(adder_1_out));  // open: cin, cout
  assign or_1_out = register_1_q | register_2_q;  // OR_Gate or_1, 16 bits wide
  assign xor_1_out = register_1_q ^ register_2_q;  // XOR_Gate xor_1, 16 bits wide
  Multiplexer #(.select(3), .width(16)) multiplexer_1 (
    .in0(adder_1_out), .in1(subtractor_1_out), .in2(and_1_out), .in3(or_1_out), .in4(xor_1_out),
    .in5(multiplier_1_out), .in6(divider_1_out), .in7({MOV, undriven}), .out(D),
    .sel(controlled_buffer_1_out[2:0]));  // open: en
  // Pins of 3 and 4 bits meet at controlled_buffer_1_out
endmodule

module PC_Controller (
  input  [15:0] Rx,
  input  [7:0] Input,
  input  [7:0] PC_input,
  input  in_4,
  input  in_5,
  input  [3:0] Opcode,
  output [7:0] Output
);

  wire clock_1_out;
  wire [7:0] adder_1_out, multiplexer_1_out;

  Multiplexer #(.width(8)) multiplexer_1 (
    .in0(PC_input), .in1(adder_1_out), .out(multiplexer_1_out), .sel(in_4));  // open: en
  Register register_1 (.D(multiplexer_1_out), .Q(Output), .clk(clock_1_out), .clr(in_5));  // open: en
  Clock clock_1 (.out(clock_1_out));
  Adder adder_1 (.a(Output), .b(Input), .out(adder_1_out));  // open: cin, cout
endmodule

module RAM (
  input  [7:0] Adress,
  input  [15:0] In,
  input  in_3,
  input  in_4,
  output [15:0] Out
);

  wire clock_1_out, not_1_out;

  not not_1 (not_1_out, in_4);
  Clock clock_1 (.out(clock_1_out));
  RAM_part #(.dataWidth(16), .bus("separate")) ram_1 (
    .addr(Adress), .din(In), .data(Out), .str(not_1_out), .sel(1'b1), .clk(clock_1_out), .ld(in_4), .clr(in_3));
endmodule

module Decoder (
  input  [15:0] Input,
  output [3:0] Opcode,
  output [7:0] Output,
  output [3:0] OO1,
  output [3:0] OO2,
  output [3:0] OO3
);

  Demultiplexer #(.select(2), .width(16)) demultiplexer_1 (.in(Input));  // open: out0, out1, out2, out3, sel, en
endmodule

module Bus_Controller (
  input  [3:0] Opcode,
  input  [15:0] Data_Input,
  input  [7:0] Immideate_Value,
  input  Clock,
  input  Clock_2,
  output ALU_Enable,
  output Register_write,
  output RAM_read,
  output RAM_write,
  output [7:0] Output
);


  assign ALU_Enable = Opcode[0];
  assign RAM_read = Opcode[2];
  assign RAM_write = Opcode[3];
  assign Register_write = Opcode[1];
endmodule
