// Logisim project lab3.circ as structural Verilog: 1 circuit, main circuit main
module main (
  input  A,
  input  B,
  input  in_3,
  input  in_4,
  input  in_5,
  input  in_6,
  input  in_7,
  input  in_8,
  input  in_9,
  input  in_10,
  input  in_11,
  input  in_12,
  input  in_13,
  input  in_14
);

  wire multiplexer_1_out, multiplexer_2_out, multiplexer_3_out, not_1_out, not_2_out, not_3_out, undriven;

  Multiplexer #(.select(3)) multiplexer_1 (
    .in0(in_4), .in1(in_6), .in2(in_5), .in3(in_7), .in4(in_8), .in5(in_9), .in6(in_10), .in7(in_11),
    .out(multiplexer_1_out), .en(in_12));  // open: sel
  not not_1 (not_1_out, A);
  not not_2 (not_2_out, in_3);
  not not_3 (not_3_out, B);
  Multiplexer #(.select(3)) multiplexer_2 (
    .in0(in_3), .in1(B), .in2(not_2_out), .in3(not_3_out), .in4(not_3_out), .in5(A), .in6(not_1_out),
    .in7(undriven), .out(multiplexer_2_out), .en(undriven));  // open: sel
  Multiplexer #(.select(3)) multiplexer_3 (
    .in0(in_3), .in1(B), .in2(not_2_out), .in3(not_3_out), .in4(A), .in5(not_1_out), .in7(undriven),
    .out(multiplexer_3_out));  // open: in6, sel, en

  assign in_13 = in_12;
  assign in_14 = in_12;

  // Notes on the sheet:
  //   Problem Number 6
  //   Problem 7
  //   cin
endmodule
