// Logisim project lab4.circ as structural Verilog: 1 circuit, main circuit main
module main (
  input  in_1,
  input  in_2,
  input  in_3,
  input  in_4
);

  wire clock_1_out, t_ff_1_q, undriven, undriven_2, undriven_3;

  Clock clock_1 (.out(clock_1_out));
  T_Flip_Flop t_ff_1 (
    .clk(clock_1_out), .T(in_1), .Q(t_ff_1_q), .preset(undriven), .reset(undriven_3), .en(undriven_2));  // open: Qn
  D_Flip_Flop d_ff_1 (
    .clk(clock_1_out), .D(in_2), .Q(t_ff_1_q), .preset(undriven), .en(undriven_2), .reset(undriven_3));  // open: Qn
  D_Flip_Flop d_ff_2 (
    .clk(clock_1_out), .D(in_3), .Q(t_ff_1_q), .preset(undriven), .en(undriven_2), .reset(undriven_3));  // open: Qn
  D_Flip_Flop d_ff_3 (
    .clk(clock_1_out), .D(in_4), .Q(t_ff_1_q), .preset(undriven), .en(undriven_2), .reset(undriven_3));  // open: Qn

  // Notes on the sheet:
  //   circuit is green
  //   Output
  //   When all the flip flops are satisfied 
endmodule
